# Fritzing sketch Display2digAlhambra (saved by Fritzing 0.9.3b)
breadboards: 1

parts:
  Q1 = NPN-Transistor [package="TO92 [THT]"]
  Parte1 = iceZUM Alhambra
  Q2 = NPN-Transistor [package="TO92 [THT]"]
  LED2 = 2-digit 7-segment [package=THT-longpads]
  R20 = Resistor [tolerance=±5% resistance=100 package="0603 [SMD]"]
  R21 = Resistor [tolerance=±5% resistance=100 package="0603 [SMD]"]
  R22 = Resistor [tolerance=±5% resistance=100 package="0603 [SMD]"]
  R23 = Resistor [tolerance=±5% resistance=100 package="0603 [SMD]"]
  R24 = Resistor [tolerance=±5% resistance=100 package="0603 [SMD]"]
  R25 = Resistor [tolerance=±5% resistance=100 package="0603 [SMD]"]
  R26 = Resistor [tolerance=±5% resistance=100 package="0603 [SMD]"]
  R27 = 220 Ω Resistor [package=THT]
  R28 = 220 Ω Resistor [package=THT]

nets:
  N1: Q1.E, Parte1.GD3, Parte1.GND, Q2.E
  N2: Q1.B, R27.Pin_0
  N3: Q1.C, LED2.DIG2
  N4: Parte1.D2, Parte1.V2, R28.Pin_1
  N5: Parte1.D3, Parte1.V3, R27.Pin_1
  N6: Parte1.GP0, Parte1.GP1, Parte1.GP5, R20.Pin_0, R21.Pin_0, R22.Pin_0
  N7: Parte1.GP2, R24.Pin_1
  N8: Parte1.GP3, R25.Pin_1
  N9: Parte1.GP4, R26.Pin_1
  N10: Parte1.GP6, R23.Pin_1
  N11: Q2.B, R28.Pin_0
  N12: Q2.C, LED2.DIG1
  N13: LED2.A, R20.Pin_1
  N14: LED2.C, R26.Pin_0
  N15: LED2.E, R25.Pin_0
  N16: LED2.D, R24.Pin_0
  N17: LED2.G, R23.Pin_0
  N18: LED2.F, R22.Pin_1
  N19: LED2.B, R21.Pin_1

notes:
  Transistoreen oinarrietan 1000 Ωeko erresistentziak konektatuko ditugu.
  Segmentuetara 100 Ωeko erresistentziak konektatuko ditugu.

custom parts:
  iceZUM Alhambra: Arduino/zum compatible Open FPGA electronic board. Synthesize hardware easily, using only open source tools
  2-digit 7-segment: Most common two-digit seven-segment led indicator you can find on the internet. 10 legs: 2 common electrodes (one per each digit), 8 electrodes of each segment.
  220 Ω Resistor: A generic resistor (0.25W)
