# Fritzing sketch 4dbhpraktika1 (saved by Fritzing 0.9.3b)
breadboards: 1

parts:
  LED1 = LED - 5mm [color="Red (633nm)" package="5 mm [THT]"]
  Part3 = iceZUM Alhambra
  R2 = Resistor [tolerance=±5% resistance=100 package="0603 [SMD]"]
  LED2 = LED - 5mm [color="Red (633nm)" package="5 mm [THT]"]
  R3 = Resistor [tolerance=±5% resistance=100 package="0603 [SMD]"]
  R4 = Resistor [tolerance=±5% resistance=10k package=THT]
  S1 = Square Pushbutton
  R5 = Resistor [tolerance=±5% resistance=100 package="0603 [SMD]"]  # not connected
  R6 = Resistor [tolerance=±5% resistance=10k package=THT]  # not connected

nets:
  N1: LED1.cathode, R2.Pin_0
  N2: LED1.anode, Part3.GP0
  N3: Part3.GD5, R2.Pin_1, R3.Pin_1, R4.Pin_1
  N4: Part3.GP2, LED2.anode
  N5: Part3.GP4, R4.Pin_0, S1.leg1
  N6: Part3.3V3, S1.leg0
  N7: LED2.cathode, R3.Pin_0

notes:
  Leden R = 100 Ω
  Pultsadorearen R = 10K

custom parts:
  iceZUM Alhambra: Arduino/zum compatible Open FPGA electronic board. Synthesize hardware easily, using only open source tools
