# Fritzing sketch Katodo4digdisplay (saved by Fritzing 0.9.3b)
breadboards: 1

parts:
  Q1 = NPN-Transistor [package="TO92 [THT]"]
  LED1 = 7-SEGMENT-4DIGIT-YOUNGSUN [package=7-segment-4digit-youngsun-longpads]
  Parte1 = iceZUM Alhambra
  Q2 = NPN-Transistor [package="TO92 [THT]"]
  Q3 = NPN-Transistor [package="TO92 [THT]"]
  Q4 = NPN-Transistor [package="TO92 [THT]"]
  R12 = 220 Ω Resistor [package=THT]
  R16 = Resistor [tolerance=±5% resistance=100 package="0603 [SMD]"]
  R17 = Resistor [tolerance=±5% resistance=100 package="0603 [SMD]"]
  R18 = Resistor [tolerance=±5% resistance=100 package="0603 [SMD]"]
  R19 = Resistor [tolerance=±5% resistance=100 package="0603 [SMD]"]
  R20 = Resistor [tolerance=±5% resistance=100 package="0603 [SMD]"]
  R21 = Resistor [tolerance=±5% resistance=100 package="0603 [SMD]"]
  R22 = Resistor [tolerance=±5% resistance=100 package="0603 [SMD]"]
  R23 = 220 Ω Resistor [package=THT]
  R24 = 220 Ω Resistor [package=THT]
  R25 = 220 Ω Resistor [package=THT]

nets:
  N1: Q1.E, Parte1.GD3, Parte1.GND, Q2.E, Q3.E, Q4.E
  N2: Q1.B, R12.Pin_0
  N3: Q1.C, LED1.B
  N4: LED1.DIG1, R19.Pin_0
  N5: LED1.DIG2, R20.Pin_0
  N6: LED1.COL-A, R21.Pin_0
  N7: LED1.E, R22.Pin_0
  N8: LED1.DIG3, Q4.C
  N9: LED1.F, R17.Pin_1
  N10: LED1.COL-C, Q3.C
  N11: LED1.C, Q2.C
  N12: LED1.A, R18.Pin_1
  N13: LED1.G, R16.Pin_1
  N14: Parte1.D0, Parte1.V0, R25.Pin_1
  N15: Parte1.D1, Parte1.V1, R24.Pin_1
  N16: Parte1.D2, Parte1.V2, R23.Pin_1
  N17: Parte1.D3, Parte1.V3, R12.Pin_1
  N18: Parte1.GP0, R16.Pin_0
  N19: Parte1.GP1, R17.Pin_0
  N20: Parte1.GP2, R21.Pin_1
  N21: Parte1.GP3, R20.Pin_1
  N22: Parte1.GP4, R19.Pin_1
  N23: Parte1.GP5, R18.Pin_0
  N24: Parte1.GP6, R22.Pin_1
  N25: Q2.B, R23.Pin_0
  N26: Q3.B, R24.Pin_0
  N27: Q4.B, R25.Pin_0

notes:
  Transistoreen oinarrietan 1000 Ωeko erresistentziak konektatuko ditugu.
  Segmentuetara 100 Ωeko erresistentziak konektatuko ditugu.

custom parts:
  iceZUM Alhambra: Arduino/zum compatible Open FPGA electronic board. Synthesize hardware easily, using only open source tools
  220 Ω Resistor: A generic resistor (0.25W)
