# Fritzing sketch LED-5V-protoboard (saved by Fritzing 0.9.3b)
breadboards: 1

parts:
  LED1 = LED - 5mm [color="Red (633nm)" package="5 mm [THT]"]
  Part3 = iceZUM Alhambra
  R1 = Resistor [tolerance=±5% resistance=220 package=THT]
  R2 = Resistor [tolerance=±5% resistance=10k package=THT]
  U1 = TRANSISTOR_NPN_2 [package=to-92]
  R3 = Resistor [tolerance=±5% resistance=220 package=THT]  # not connected
  R4 = Resistor [tolerance=±5% resistance=10k package=THT]  # not connected
  U2 = TRANSISTOR_NPN_2 [package=to-92]  # not connected

nets:
  N1: LED1.cathode, R1.Pin_0
  N2: LED1.anode, Part3.V13#32
  N3: Part3.G13, U1.E
  N4: Part3.V13#46, R2.Pin_1
  N5: R1.Pin_1, U1.C
  N6: R2.Pin_0, U1.B

notes:
  NPN BC547B
  R = 10k
  R = 220 Ω

custom parts:
  iceZUM Alhambra: Arduino/zum compatible Open FPGA electronic board. Synthesize hardware easily, using only open source tools
