# Fritzing sketch pultsadorea-3v3-breadboard (saved by Fritzing 0.9.3b)
breadboards: 1

parts:
  Part1 = iceZUM Alhambra
  S1 = Momentary Switch [package=ksa_sealed_tac_switch]
  R1 = Resistor [tolerance=±5% resistance=10k package=THT]

nets:
  N1: Part1.GD5, R1.Pin_1
  N2: Part1.GP0, S1.1, R1.Pin_0
  N3: Part1.3V3, S1.3

notes:
  R=10K

custom parts:
  iceZUM Alhambra: Arduino/zum compatible Open FPGA electronic board. Synthesize hardware easily, using only open source tools
