# Fritzing sketch pultsadorea-5v-breadboard (saved by Fritzing 0.9.3b)
breadboards: 1

parts:
  Part1 = iceZUM Alhambra
  S1 = Momentary Switch [package=ksa_sealed_tac_switch]
  R1 = Resistor [tolerance=±5% resistance=1k package=THT]

nets:
  N1: Part1.D0, Part1.V0#59, S1.1, R1.Pin_0
  N2: Part1.G0, R1.Pin_1
  N3: Part1.V0#45, S1.3

notes:
  R= 1K

custom parts:
  iceZUM Alhambra: Arduino/zum compatible Open FPGA electronic board. Synthesize hardware easily, using only open source tools
