# Fritzing sketch rgbAnodo (saved by Fritzing 0.9.3b)
breadboards: 1

parts:
  Part1 = iceZUM Alhambra
  LED1 = RGB LED - (4 legs) [package="5 mm [THT]"]
  R4 = Resistor [tolerance=±5% resistance=100 package="0603 [SMD]"]  # not connected
  R5 = Resistor [tolerance=±5% resistance=100 package="0603 [SMD]"]
  R6 = Resistor [tolerance=±5% resistance=100 package="0603 [SMD]"]
  R7 = Resistor [tolerance=±5% resistance=100 package="0603 [SMD]"]

nets:
  N1: Part1.GP0, R5.Pin_1
  N2: Part1.GP1, R7.Pin_1
  N3: Part1.GP3, R6.Pin_1
  N4: Part1.3V3, LED1.common_anode
  N5: LED1.red_cathode, R7.Pin_0
  N6: LED1.green_cathode, R5.Pin_0
  N7: LED1.blue_cathode, R6.Pin_0

notes:
  RGBaren 1.(gorria), 3.(berdea) eta 4. (urdina) borneei 100 Ωeko erresistentzia konektatzen zaie seriean.
  RGBaren 2. bornea plakaren 3,3 Vra konektatuko da.
  Anodo komuneko RGBa

custom parts:
  iceZUM Alhambra: Arduino/zum compatible Open FPGA electronic board. Synthesize hardware easily, using only open source tools
